# Fritzing sketch LIXIE (saved by Fritzing 0.9.3b)

parts:
  Part2 = ws2812b [package="smd 2812b"]
  Part3 = ws2812b [package="smd 2812b"]
  Part4 = ws2812b [package="smd 2812b"]
  Part5 = ws2812b [package="smd 2812b"]
  Part6 = ws2812b [package="smd 2812b"]
  Part7 = ws2812b [package="smd 2812b"]
  Part8 = ws2812b [package="smd 2812b"]
  Part9 = ws2812b [package="smd 2812b"]
  Part10 = ws2812b [package="smd 2812b"]
  Part11 = ws2812b [package="smd 2812b"]
  Part12 = ws2812b [package="smd 2812b"]
  Part13 = ws2812b [package="smd 2812b"]
  Part14 = ws2812b [package="smd 2812b"]
  Part15 = ws2812b [package="smd 2812b"]
  Part16 = ws2812b [package="smd 2812b"]
  Part17 = ws2812b [package="smd 2812b"]
  Part18 = ws2812b [package="smd 2812b"]
  Part19 = ws2812b [package="smd 2812b"]
  Part20 = ws2812b [package="smd 2812b"]
  Part21 = ws2812b [package="smd 2812b"]
  C1 = Electrolytic Capacitor [capacitance=100µF package="200 mil [THT, electrolytic]"]
  Part1 = Arduino Uno (Rev3)

nets:
  VDD: Part2.VDD, Part3.VDD, Part4.VDD, Part5.VDD, Part6.VDD, Part7.VDD, Part8.VDD, Part9.VDD, Part10.VDD, Part11.VDD, Part12.VDD, Part13.VDD, Part14.VDD, Part15.VDD, Part16.VDD, Part17.VDD, Part18.VDD, Part19.VDD, Part20.VDD, Part21.VDD, C1.+, Part1.5V
  N1: Part2.DOUT, Part3.DIN
  VSS: Part2.VSS, Part3.VSS, Part4.VSS, Part5.VSS, Part6.VSS, Part7.VSS, Part8.VSS, Part9.VSS, Part10.VSS, Part11.VSS, Part12.VSS, Part13.VSS, Part14.VSS, Part15.VSS, Part16.VSS, Part17.VSS, Part18.VSS, Part19.VSS, Part20.VSS, Part21.VSS
  N2: Part2.DIN, Part1.D11_PWM/MOSI
  N3: Part3.DOUT, Part4.DIN
  N4: Part4.DOUT, Part6.DIN
  N5: Part5.DOUT, Part8.DIN
  N6: Part5.DIN, Part6.DOUT
  N7: Part7.DOUT, Part10.DIN
  N8: Part7.DIN, Part9.DOUT
  N9: Part8.DOUT, Part9.DIN
  N10: Part10.DOUT, Part11.DIN
  N11: Part11.DOUT, Part21.DIN
  N12: Part12.DOUT, Part16.DIN
  N13: Part12.DIN, Part13.DOUT
  N14: Part13.DIN, Part17.DOUT
  N15: Part14.DOUT, Part19.DIN
  N16: Part14.DIN, Part15.DOUT
  N17: Part15.DIN, Part20.DOUT
  N18: Part17.DIN, Part18.DOUT
  N19: Part18.DIN, Part19.DOUT
  N20: Part20.DIN, Part21.DOUT
  N21: C1.-, Part1.GND
